// Logisim project DESIGN_CPU.circ as structural Verilog: 10 circuits, main circuit main
module main (
  input  [7:0] in_1,
  input  in_2,
  input  in_3,
  output [7:0] out_4
);

  CPU_REG_8 cpu_reg_8_1 (.in_1(in_1), .out_4(out_4), .in_2(in_3), .in_3(in_2));
endmodule

module CPU_MEM_8 (
  input  [7:0] i,
  input  s,
  output [7:0] o
);

  CPU_MEM_1 cpu_mem_1_1 (.s(i[0]), .e_2(o[0]), .e(s));
  CPU_MEM_1 cpu_mem_1_2 (.s(i[1]), .e_2(o[1]), .e(s));
  CPU_MEM_1 cpu_mem_1_3 (.s(i[2]), .e_2(o[2]), .e(s));
  CPU_MEM_1 cpu_mem_1_4 (.s(i[3]), .e_2(o[3]), .e(s));
  CPU_MEM_1 cpu_mem_1_5 (.s(i[4]), .e_2(o[4]), .e(s));
  CPU_MEM_1 cpu_mem_1_6 (.s(i[5]), .e_2(o[5]), .e(s));
  CPU_MEM_1 cpu_mem_1_7 (.s(i[6]), .e_2(o[6]), .e(s));
  CPU_MEM_1 cpu_mem_1_8 (.s(i[7]), .e_2(o[7]), .e(s));
endmodule

module CPU_ENABLE (
  input  [7:0] in_1,
  input  in_2,
  output [7:0] out_3
);

  and and_1 (out_3[0], in_1[0], in_2);
  and and_2 (out_3[1], in_1[1], in_2);
  and and_3 (out_3[2], in_1[2], in_2);
  and and_4 (out_3[3], in_1[3], in_2);
  and and_5 (out_3[4], in_1[4], in_2);
  and and_6 (out_3[5], in_1[5], in_2);
  and and_7 (out_3[6], in_1[6], in_2);
  and and_8 (out_3[7], in_1[7], in_2);
endmodule

module CPU_REG_8 (
  input  [7:0] in_1,
  input  in_2,
  input  in_3,
  output [7:0] out_4
);

  wire [7:0] cpu_mem_8_1_o;

  CPU_MEM_8 cpu_mem_8_1 (.i(in_1), .s(in_2), .o(cpu_mem_8_1_o));
  CPU_ENABLE cpu_enable_1 (.out_3(out_4), .in_1(cpu_mem_8_1_o), .in_2(in_3));
endmodule

module CPU_DECODER_2X4 (
  input  in_1,
  input  in_2,
  output out_3,
  output out_4,
  output out_5,
  output out_6
);

  wire not_1_out, not_2_out;

  not not_1 (not_1_out, in_1);
  not not_2 (not_2_out, in_2);
  and and_1 (out_3, not_1_out, not_2_out);
  and and_2 (out_4, not_1_out, in_2);
  and and_3 (out_5, in_1, not_2_out);
  and and_4 (out_6, in_1, in_2);
endmodule

module CPU_DECODER_4X16 (
  input  [3:0] \input ,
  input  enable,
  output [15:0] out_3
);

  wire cpu_decoder_2x4e_1_out_4, cpu_decoder_2x4e_1_out_5, cpu_decoder_2x4e_1_out_6, cpu_decoder_2x4e_1_out_7;

  CPU_DECODER_2X4E cpu_decoder_2x4e_1 (
    .in_3(1'b1), .out_4(cpu_decoder_2x4e_1_out_4), .out_5(cpu_decoder_2x4e_1_out_5),
    .out_6(cpu_decoder_2x4e_1_out_6), .out_7(cpu_decoder_2x4e_1_out_7), .in_1(\input [2]), .in_2(\input [3]));
  CPU_DECODER_2X4E cpu_decoder_2x4e_2 (
    .in_3(cpu_decoder_2x4e_1_out_4), .out_4(out_3[0]), .out_5(out_3[1]), .out_6(out_3[2]), .out_7(out_3[3]),
    .in_1(\input [0]), .in_2(\input [1]));
  CPU_DECODER_2X4E cpu_decoder_2x4e_3 (
    .in_3(cpu_decoder_2x4e_1_out_5), .out_4(out_3[4]), .out_5(out_3[5]), .out_6(out_3[6]), .out_7(out_3[7]),
    .in_1(\input [0]), .in_2(\input [1]));
  CPU_DECODER_2X4E cpu_decoder_2x4e_4 (
    .in_3(cpu_decoder_2x4e_1_out_6), .out_4(out_3[8]), .out_5(out_3[9]), .out_6(out_3[10]),
    .out_7(out_3[11]), .in_1(\input [0]), .in_2(\input [1]));
  CPU_DECODER_2X4E cpu_decoder_2x4e_5 (
    .in_3(cpu_decoder_2x4e_1_out_7), .out_4(out_3[12]), .out_5(out_3[13]), .out_6(out_3[14]),
    .out_7(out_3[15]), .in_1(\input [0]), .in_2(\input [1]));
endmodule

module CPU_DECODER_2X4E (
  input  in_1,
  input  in_2,
  input  in_3,
  output out_4,
  output out_5,
  output out_6,
  output out_7
);

  wire not_1_out, not_2_out;

  not not_1 (not_1_out, in_1);
  not not_2 (not_2_out, in_2);
  and and_1 (out_4, in_3, not_1_out, not_2_out);
  and and_2 (out_5, in_3, not_1_out, in_2);
  and and_3 (out_6, in_3, in_1, not_2_out);
  and and_4 (out_7, in_1, in_3, in_2);
endmodule

module CPU_REG_BYTE (
  input  [7:0] in_1,
  input  reset,
  input  h,
  input  v,
  input  s,
  input  e,
  output [7:0] \output 
);

  wire and_1_out, and_2_out, and_3_out, or_1_out;
  wire [7:0] cpu_reg_8_1_out_4;

  and and_1 (and_1_out, h, v);
  and and_2 (and_2_out, and_1_out, s);
  and and_3 (and_3_out, and_1_out, e);
  or or_1 (or_1_out, reset, and_2_out);
  CPU_REG_8 cpu_reg_8_1 (.in_1(in_1), .out_4(cpu_reg_8_1_out_4), .in_2(or_1_out), .in_3(and_3_out));
  CPU_BUFFER_8 cpu_buffer_8_1 (.\input (cpu_reg_8_1_out_4), .enable(and_3_out), .\output (\output ));
endmodule

module CPU_BUFFER_8 (
  input  [7:0] \input ,
  input  enable,
  output [7:0] \output 
);

  and and_1 (\output [0], \input [0], enable);
  and and_2 (\output [1], \input [1], enable);
  and and_3 (\output [2], \input [2], enable);
  and and_4 (\output [3], \input [3], enable);
  and and_5 (\output [4], \input [4], enable);
  and and_6 (\output [5], \input [5], enable);
  and and_7 (\output [6], \input [6], enable);
  and and_8 (\output [7], \input [7], enable);
endmodule

module CPU_RAM_16 (
  input  [7:0] in_1,
  input  [7:0] \input ,
  input  reset,
  input  set,
  input  enable,
  output [7:0] out_6,
  output [7:0] out_7,
  output [7:0] out_8,
  output [7:0] out_9,
  output [7:0] out_10,
  output [7:0] out_11,
  output [7:0] out_12,
  output [7:0] out_13,
  output [7:0] out_14,
  output [7:0] out_15,
  output [7:0] out_16,
  output [7:0] out_17,
  output [7:0] out_18,
  output [7:0] out_19,
  output [7:0] out_20,
  output [7:0] out_21
);

  wire [15:0] cpu_decoder_4x16_1_out_3, cpu_decoder_4x16_2_out_3;

  CPU_DECODER_4X16 cpu_decoder_4x16_1 (.out_3(cpu_decoder_4x16_1_out_3), .\input (in_1[7:4]));  // open: enable
  CPU_REG_BYTE cpu_reg_byte_1 (
    .reset(reset), .h(cpu_decoder_4x16_1_out_3[0]), .v(cpu_decoder_4x16_2_out_3[15]), .in_1(\input ),
    .\output (out_6), .s(set), .e(enable));
  CPU_REG_BYTE cpu_reg_byte_2 (
    .reset(reset), .h(cpu_decoder_4x16_1_out_3[0]), .v(cpu_decoder_4x16_2_out_3[14]), .in_1(\input ),
    .\output (out_7), .s(set), .e(enable));
  CPU_REG_BYTE cpu_reg_byte_3 (
    .reset(reset), .h(cpu_decoder_4x16_1_out_3[0]), .v(cpu_decoder_4x16_2_out_3[13]), .in_1(\input ),
    .\output (out_8), .s(set), .e(enable));
  CPU_DECODER_4X16 cpu_decoder_4x16_2 (.out_3(cpu_decoder_4x16_2_out_3), .\input (in_1[3:0]));  // open: enable
  CPU_REG_BYTE cpu_reg_byte_4 (
    .reset(reset), .h(cpu_decoder_4x16_1_out_3[0]), .v(cpu_decoder_4x16_2_out_3[12]), .in_1(\input ),
    .\output (out_9), .s(set), .e(enable));
  CPU_REG_BYTE cpu_reg_byte_5 (
    .reset(reset), .h(cpu_decoder_4x16_1_out_3[0]), .v(cpu_decoder_4x16_2_out_3[11]), .in_1(\input ),
    .\output (out_10), .s(set), .e(enable));
  CPU_REG_BYTE cpu_reg_byte_6 (
    .reset(reset), .h(cpu_decoder_4x16_1_out_3[0]), .v(cpu_decoder_4x16_2_out_3[10]), .\output (out_11),
    .s(set), .e(enable));  // open: in_1
  CPU_REG_BYTE cpu_reg_byte_7 (
    .reset(reset), .h(cpu_decoder_4x16_1_out_3[0]), .v(cpu_decoder_4x16_2_out_3[9]), .in_1(\input ),
    .\output (out_12), .s(set), .e(enable));
  CPU_REG_BYTE cpu_reg_byte_8 (
    .reset(reset), .h(cpu_decoder_4x16_1_out_3[0]), .v(cpu_decoder_4x16_2_out_3[8]), .in_1(\input ),
    .\output (out_13), .s(set), .e(enable));
  CPU_REG_BYTE cpu_reg_byte_9 (
    .reset(reset), .h(cpu_decoder_4x16_1_out_3[0]), .v(cpu_decoder_4x16_2_out_3[7]), .in_1(\input ),
    .\output (out_14), .s(set), .e(enable));
  CPU_REG_BYTE cpu_reg_byte_10 (
    .reset(reset), .h(cpu_decoder_4x16_1_out_3[0]), .v(cpu_decoder_4x16_2_out_3[6]), .in_1(\input ),
    .\output (out_15), .s(set), .e(enable));
  CPU_REG_BYTE cpu_reg_byte_11 (
    .reset(reset), .h(cpu_decoder_4x16_1_out_3[0]), .v(cpu_decoder_4x16_2_out_3[5]), .in_1(\input ),
    .\output (out_16), .s(set), .e(enable));
  CPU_REG_BYTE cpu_reg_byte_12 (
    .reset(reset), .h(cpu_decoder_4x16_1_out_3[0]), .v(cpu_decoder_4x16_2_out_3[4]), .in_1(\input ),
    .\output (out_17), .s(set), .e(enable));
  CPU_REG_BYTE cpu_reg_byte_13 (
    .reset(reset), .h(cpu_decoder_4x16_1_out_3[0]), .v(cpu_decoder_4x16_2_out_3[3]), .in_1(\input ),
    .\output (out_18), .s(set), .e(enable));
  CPU_REG_BYTE cpu_reg_byte_14 (
    .reset(reset), .h(cpu_decoder_4x16_1_out_3[0]), .v(cpu_decoder_4x16_2_out_3[2]), .in_1(\input ),
    .\output (out_19), .s(set), .e(enable));
  CPU_REG_BYTE cpu_reg_byte_15 (
    .reset(reset), .h(cpu_decoder_4x16_1_out_3[0]), .v(cpu_decoder_4x16_2_out_3[1]), .in_1(\input ),
    .\output (out_20), .s(set), .e(enable));
  CPU_REG_BYTE cpu_reg_byte_16 (
    .reset(reset), .h(cpu_decoder_4x16_1_out_3[0]), .v(cpu_decoder_4x16_2_out_3[0]), .in_1(\input ),
    .\output (out_21), .s(set), .e(enable));
endmodule
